// Logisim project MIPS.circ as structural Verilog: 6 circuits, main circuit MIPS
module MIPS (
  input  in_1
);

  wire and_1_out, and_2_out, clock_1_out, control_1_alu_src, control_1_beq, control_1_bneq, control_1_jump,
       control_1_memread, control_1_memtoreg, control_1_memwrite, control_1_regdst, control_1_regwrite,
       main_1_p4, not_1_out, or_1_out, shift_logical_unit_1_value;
  wire [2:0] control_1_alu_op;
  wire [3:0] multiplexer_1_out;
  wire [7:0] adder_1_out, adder_2_out, bit_extender_1_out, data_memory_1_output_data,
       instruction_1_instruction_2, instruction_1_instruction_3, main_1_p1, main_1_p5, multiplexer_2_out,
       multiplexer_4_out, multiplexer_5_out, multiplexer_6_out, register_1_q, register_2_read_1_data,
       register_2_read_2_data, register_2_sp, register_2_t0, register_2_t1, register_2_t2, register_2_t3,
       register_2_t4, register_2_t5;
  wire [19:16] instruction_1_instruction;

  // Probe on register_2_t4
  // Probe on register_2_t3
  // Probe on register_2_t2
  // Probe on register_2_t1
  // Probe on register_2_t0
  Clock clock_1 (.out(clock_1_out));
  // Probe on multiplexer_6_out
  Register_part #(.trigger("falling")) register_1 (
    .D(multiplexer_6_out), .Q(register_1_q), .clk(clock_1_out), .clr(in_1));  // open: en
  // Probe on register_1_q
  // Probe on {instruction_1_instruction, instruction_1_instruction_3, instruction_1_instruction_2}
  Instruction instruction_1 (
    .Read_Address(register_1_q),
    .Instruction({instruction_1_instruction, instruction_1_instruction_3, instruction_1_instruction_2}));
  Multiplexer #(.width(4), .enable("false")) multiplexer_1 (
    .in0(instruction_1_instruction_3[3:0]), .in1(instruction_1_instruction_2[7:4]), .out(multiplexer_1_out),
    .sel(control_1_regdst));
  Control control_1 (
    .OP_CODE(instruction_1_instruction), .RegWrite(control_1_regwrite), .ALU_Src(control_1_alu_src),
    .MemWrite(control_1_memwrite), .ALU_op(control_1_alu_op), .MemToReg(control_1_memtoreg),
    .MemRead(control_1_memread), .Bneq(control_1_bneq), .Beq(control_1_beq), .Jump(control_1_jump),
    .RegDst(control_1_regdst));
  assign bit_extender_1_out = {{4{1'b0}}, instruction_1_instruction_2[3:0]};  // Bit_Extender bit_extender_1
  Register register_2 (
    .Read_1_Address(instruction_1_instruction_3[7:4]), .Write_Data(multiplexer_5_out),
    .RegWrite(control_1_regwrite), .Clk(clock_1_out), .Write_Address(multiplexer_1_out),
    .Read_2_Address(instruction_1_instruction_3[3:0]), .Read_1_Data(register_2_read_1_data),
    .Read_2_Data(register_2_read_2_data), .t0(register_2_t0), .t1(register_2_t1), .t2(register_2_t2),
    .t3(register_2_t3), .t4(register_2_t4), .t5(register_2_t5), .sp(register_2_sp));
  Shift_Logical_unit shift_logical_unit_1 (.Op_code(instruction_1_instruction), .Value(shift_logical_unit_1_value));
  Adder adder_1 (.a(register_1_q), .b(8'h1), .out(adder_1_out));  // open: cin, cout
  Multiplexer #(.width(8), .enable("false")) multiplexer_2 (
    .in0(register_2_read_2_data), .in1(instruction_1_instruction_2), .out(multiplexer_2_out),
    .sel(control_1_alu_src));
  Adder adder_2 (.a(adder_1_out), .b(instruction_1_instruction_2), .out(adder_2_out));  // open: cin, cout
  // alooo_main main_1: pin names not known; wires that end beside it: main_1_p1, multiplexer_2_out, control_1_alu_op, main_1_p4, main_1_p5
  Multiplexer #(.width(8), .enable("false")) multiplexer_3 (
    .in0(register_2_read_1_data), .in1(bit_extender_1_out), .out(main_1_p1), .sel(shift_logical_unit_1_value));
  not not_1 (not_1_out, main_1_p4);
  // Probe on register_2_t5
  // Probe on register_2_sp
  and and_1 (and_1_out, control_1_beq, main_1_p4);
  and and_2 (and_2_out, control_1_bneq, not_1_out);
  or or_1 (or_1_out, and_1_out, and_2_out);
  Data_Memory data_memory_1 (
    .Address(main_1_p5), .Write_Data(register_2_read_2_data), .Output_Data(data_memory_1_output_data),
    .MemWrite(control_1_memwrite), .Clk(clock_1_out), .MemRead(control_1_memread));
  Multiplexer #(.width(8), .enable("false")) multiplexer_4 (
    .in0(adder_1_out), .in1(adder_2_out), .out(multiplexer_4_out), .sel(or_1_out));
  Multiplexer #(.width(8), .enable("false")) multiplexer_5 (
    .in0(main_1_p5), .in1(data_memory_1_output_data), .out(multiplexer_5_out), .sel(control_1_memtoreg));
  Multiplexer #(.width(8), .enable("false")) multiplexer_6 (
    .in0(multiplexer_4_out), .in1(instruction_1_instruction_3), .out(multiplexer_6_out), .sel(control_1_jump));
endmodule

module Instruction (
  input  [7:0] Read_Address,
  output [19:0] Instruction
);

  ROM #(.dataWidth(20)) rom_1 (.addr(Read_Address), .data(Instruction));  // open: sel

  // Notes on the sheet:
  //   contents of rom_1 (hex, n*v repeats v):
  //   366ff 3710a 37205 11200 10230 13040 42103 50111 81301 61e00 c4040 b1102 90331 a2103 e1300 20420
  //   61d00 46000 b6601 46200 b6601 d0005 36601 a6000 72214 36601 a6200 2220 61e00 f02f3
endmodule

module Data_Memory (
  input  [7:0] Address,
  input  [7:0] Write_Data,
  input  MemRead,
  input  MemWrite,
  input  Clk,
  output [7:0] Output_Data
);

  RAM #(.bus("separate")) ram_1 (
    .addr(Address), .din(Write_Data), .data(Output_Data), .str(MemWrite), .clk(Clk), .ld(MemRead));  // open: sel, clr
endmodule

module Register (
  input  [3:0] Read_1_Address,
  input  [7:0] Write_Data,
  input  RegWrite,
  input  Clk,
  input  [3:0] Write_Address,
  input  [3:0] Read_2_Address,
  output [7:0] Read_1_Data,
  output [7:0] Read_2_Data,
  output [7:0] t0,
  output [7:0] t1,
  output [7:0] t2,
  output [7:0] t3,
  output [7:0] t4,
  output [7:0] t5,
  output [7:0] sp
);

  wire and_1_out, demultiplexer_1_out0, demultiplexer_1_out1, demultiplexer_1_out2, demultiplexer_1_out3,
       demultiplexer_1_out4, demultiplexer_1_out5, demultiplexer_1_out6;
  wire [7:0] zero_q;

  and and_1 (and_1_out, RegWrite, Clk);
  Demultiplexer #(.select(3), .enable("false")) demultiplexer_1 (
    .out0(demultiplexer_1_out0), .out1(demultiplexer_1_out1), .out2(demultiplexer_1_out2),
    .out3(demultiplexer_1_out3), .out4(demultiplexer_1_out4), .out5(demultiplexer_1_out5),
    .out6(demultiplexer_1_out6), .in(and_1_out), .sel(Write_Address[2:0]));  // open: out7
  Register_part zero (.D({8{1'b0}}), .Q(zero_q), .clk(1'b0));  // open: en, clr
  Register_part u_t0 (.D(Write_Data), .Q(t0), .clk(demultiplexer_1_out0));  // open: en, clr
  Register_part u_t1 (.D(Write_Data), .Q(t1), .clk(demultiplexer_1_out1));  // open: en, clr
  Register_part u_t2 (.D(Write_Data), .Q(t2), .clk(demultiplexer_1_out2));  // open: en, clr
  Register_part u_t3 (.D(Write_Data), .Q(t3), .clk(demultiplexer_1_out3));  // open: en, clr
  Register_part u_t4 (.D(Write_Data), .Q(t4), .clk(demultiplexer_1_out4));  // open: en, clr
  Register_part u_t5 (.D(Write_Data), .Q(t5), .clk(demultiplexer_1_out5));  // open: en, clr
  Register_part u_sp (.D(Write_Data), .Q(sp), .clk(demultiplexer_1_out6));  // open: en, clr
  Multiplexer #(.select(3), .width(8), .disabled(0), .enable("false")) multiplexer_1 (
    .in0(t0), .in1(t1), .in2(t2), .in3(t3), .in4(t4), .in5(t5), .in6(sp), .in7(zero_q), .out(Read_1_Data),
    .sel(Read_1_Address[2:0]));
  Multiplexer #(.select(3), .width(8), .disabled(0), .enable("false")) multiplexer_2 (
    .in0(t0), .in1(t1), .in2(t2), .in3(t3), .in4(t4), .in5(t5), .in6(sp), .in7(zero_q), .out(Read_2_Data),
    .sel(Read_2_Address[2:0]));
endmodule

module Control (
  input  [3:0] OP_CODE,
  output RegWrite,
  output ALU_Src,
  output MemWrite,
  output [2:0] ALU_op,
  output MemToReg,
  output MemRead,
  output Bneq,
  output Beq,
  output Jump,
  output RegDst
);

  ROM #(.addrWidth(4), .dataWidth(12)) rom_1 (
    .addr(OP_CODE), .data({RegDst, Jump, Beq, Bneq, MemRead, MemToReg, ALU_op, MemWrite, ALU_Src, RegWrite}));  // open: sel

  // Notes on the sheet:
  //   contents of rom_1 (hex, n*v repeats v):
  //   821 801 811 3 6 829 400 1b 208 831 c3 b 809 13 819 108
endmodule

module Shift_Logical_unit (
  input  [3:0] Op_code,
  output Value
);

  wire and_1_out, and_2_out, not_1_out, not_2_out, not_3_out, not_4_out;

  not not_1 (not_1_out, Op_code[1]);
  not not_2 (not_2_out, Op_code[3]);
  not not_3 (not_3_out, Op_code[1]);
  not not_4 (not_4_out, Op_code[2]);
  and and_1 (and_1_out, Op_code[0], not_1_out, Op_code[2], not_2_out);
  and and_2 (and_2_out, Op_code[0], not_3_out, not_4_out, Op_code[3]);
  or or_1 (Value, and_1_out, and_2_out);
endmodule
